# Fritzing sketch MP2_Diagram (saved by Fritzing 0.9.5d)
breadboards: 1

parts:
  ESP32 = Arduino Leonardo (Rev3b)
  Accelerometer = Triple Axis Accelerometer Breakout - ADXL345
  Piezo_Buzzer = Piezo Speaker
  Left_Button = Pushbutton [package="[THT]"]
  Right_Button = Pushbutton [package="[THT]"]
  R1 = Resistor [tolerance=±5% resistance=1k package=THT]
  Transistor = TRANSISTOR_NPN [package=to-92]
  Joystick = Thumb Joystick
  Vibromotor = Lilypad Vibe Motor
  Grove1 = Grove OLED 128x96

nets:
  N1: ESP32.D2/SDA, Grove1.SDA
  N2: ESP32.D3_PWM/SCL, Grove1.SCL
  N3: ESP32.D6_PWM/A7, Left_Button.Pin_3, Left_Button.Pin_4
  N4: ESP32.D7, Right_Button.Pin_3, Right_Button.Pin_4
  3V3: ESP32.3V3, Joystick.VCC
  GND: ESP32.GND, Accelerometer.GND, Piezo_Buzzer.pin1, Left_Button.Pin_2, Right_Button.Pin_1, Right_Button.Pin_2, Transistor.E, Joystick.GND, Grove1.GND
  N5: ESP32.A0, Joystick.VERT
  N6: ESP32.D8/A8, R1.Pin_0
  N7: ESP32.D9_PWM/A9, Piezo_Buzzer.pin2
  N8: ESP32.D10_PWM/A10, Accelerometer.SCL
  N9: ESP32.D11_PWM, Accelerometer.SDA
  N10: ESP32.D12/A11, Accelerometer.SDO
  N11: ESP32.D13_PWM, Accelerometer.CS
  VCC: Accelerometer.VCC, Vibromotor.Supply, Grove1.VCC
  N12: R1.Pin_1, Transistor.B
  N13: Transistor.C, Vibromotor.GND
